# Fritzing sketch Untitled Sketch (saved by Fritzing 0.9.3b)
breadboards: 2

parts:
  Part1 = Arduino Uno (Rev3)
  NRF_2_4GHZ = NRF24L01+ Breakout Board
  DHT11 = DHT11 module
  C2 = Electrolytic Capacitor [capacitance=10μF package="0605 [SMD, electrolytic]"]
  Part4 = Arduino Uno (Rev3)
  NRF_2_4GHZ_2 = NRF24L01+ Breakout Board
  C3 = Electrolytic Capacitor [capacitance=10μF package="0605 [SMD, electrolytic]"]
  LCD1 = LCD screen
  U1 = POT [package=pot_mammoth]

nets:
  N1: Part1.D8, NRF_2_4GHZ.CS
  N2: Part1.D9_PWM, NRF_2_4GHZ.CE
  N3: Part1.D11_PWM/MOSI, NRF_2_4GHZ.MOSI
  N4: Part1.D12/MISO, NRF_2_4GHZ.MISO
  N5: Part1.D13/SCK, NRF_2_4GHZ.SCK
  GND: Part1.GND, NRF_2_4GHZ.GND, C2.-, LCD1.VSS, LCD1.LED-, U1.S
  N6: Part1.D2, LCD1.DB7
  N7: Part1.D3_PWM, LCD1.DB6
  N8: Part1.D4, LCD1.DB5
  N9: Part1.D5_PWM, LCD1.DB4
  N10: Part1.D6_PWM, LCD1.E
  N11: Part1.D7, LCD1.RS
  3V3: Part1.3V3, NRF_2_4GHZ.VCC, C2.+
  5V: Part1.5V, LCD1.VDD, LCD1.LED+
  VCC: DHT11.VCC, Part4.3V3, NRF_2_4GHZ_2.VCC, C3.+
  GND_2: DHT11.GND, Part4.GND, NRF_2_4GHZ_2.GND, C3.-
  N12: DHT11.DATA, Part4.D2
  N13: Part4.D8, NRF_2_4GHZ_2.CS
  N14: Part4.D9_PWM, NRF_2_4GHZ_2.CE
  N15: Part4.D11_PWM/MOSI, NRF_2_4GHZ_2.MOSI
  N16: Part4.D12/MISO, NRF_2_4GHZ_2.MISO
  N17: Part4.D13/SCK, NRF_2_4GHZ_2.SCK
  N18: LCD1.V0, U1.A

custom parts:
  DHT11 module: https://cdn-learn.adafruit.com/downloads/pdf/dht.pdf DHT11 black pcb module reference by:https://github.com/adafruit/Fritzing-Library/blob/master/parts/DHT11%20Humitidy%20and%20Temperature%20Sensor.fzpz
  LCD screen: A standard character display, usually with 2x16 characters. Comes in many colors.
